// Logisim project add.circ as structural Verilog: 5 circuits, main circuit fulladd_1bit
module fulladd_1bit (
  input  A,
  input  B,
  input  CIN,
  output SUM,
  output COUT
);

  wire and_1_out, and_2_out, and_3_out;

  and and_1 (and_1_out, A, B);
  and and_2 (and_2_out, CIN, A);
  and and_3 (and_3_out, B, CIN);
  ExactlyOne xor_1 (.out(SUM), .in0(A), .in1(B), .in2(CIN));
  or or_1 (COUT, and_1_out, and_2_out, and_3_out);
endmodule

module half_add (
  input  A,
  input  B,
  output COUT,
  output SUM
);

  wire and_2_out, and_3_out, not_1_out, not_2_out;

  not not_1 (not_1_out, A);
  not not_2 (not_2_out, B);
  and and_1 (COUT, A, B);
  and and_2 (and_2_out, B, not_1_out);
  and and_3 (and_3_out, A, not_2_out);
  or or_1 (SUM, and_2_out, and_3_out);
endmodule

module fulladdwithhalf_1bit (
  input  A,
  input  B,
  input  CIN,
  output cout,
  output sum
);

  wire half_add_1_cout, half_add_1_sum, half_add_2_cout;

  half_add half_add_1 (.A(A), .B(B), .COUT(half_add_1_cout), .SUM(half_add_1_sum));
  half_add half_add_2 (.A(half_add_1_sum), .B(CIN), .COUT(half_add_2_cout), .SUM(sum));
  or or_1 (cout, half_add_1_cout, half_add_2_cout);
endmodule

module fulladd4bit (
  input  [3:0] A,
  input  Cin,
  input  [3:0] B,
  output [3:0] Sum,
  output Cout
);

  wire fulladd_1bit_1_cout, fulladd_1bit_2_cout, fulladd_1bit_3_cout;

  fulladd_1bit fulladd_1bit_1 (.A(A[0]), .B(B[0]), .CIN(Cin), .SUM(Sum[0]), .COUT(fulladd_1bit_1_cout));
  fulladd_1bit fulladd_1bit_2 (.A(A[1]), .B(B[1]), .CIN(fulladd_1bit_1_cout), .SUM(Sum[1]), .COUT(fulladd_1bit_2_cout));
  fulladd_1bit fulladd_1bit_3 (.A(A[2]), .B(B[2]), .CIN(fulladd_1bit_2_cout), .SUM(Sum[2]), .COUT(fulladd_1bit_3_cout));
  fulladd_1bit fulladd_1bit_4 (.A(A[3]), .B(B[3]), .CIN(fulladd_1bit_3_cout), .SUM(Sum[3]), .COUT(Cout));
endmodule

module fulladd_4bit_display (
);

  wire CIN_sw1, decoder_7_segmenthex_1_a_display, decoder_7_segmenthex_1_b_display,
       decoder_7_segmenthex_1_c_display, decoder_7_segmenthex_1_d_display, decoder_7_segmenthex_1_e_display,
       decoder_7_segmenthex_1_f_display, decoder_7_segmenthex_1_g_display;
  wire [3:0] A_sw1, B_sw1, fulladd4bit_1_sum;

  DipSwitch #(.number(4)) A (.sw1(A_sw1[0]), .sw2(A_sw1[1]), .sw3(A_sw1[2]), .sw4(A_sw1[3]));
  DipSwitch #(.number(4)) B (.sw1(B_sw1[0]), .sw2(B_sw1[1]), .sw3(B_sw1[2]), .sw4(B_sw1[3]));
  DipSwitch #(.number(1)) CIN (.sw1(CIN_sw1));
  fulladd4bit fulladd4bit_1 (.A(A_sw1), .Cin(CIN_sw1), .B(B_sw1), .Sum(fulladd4bit_1_sum));  // open: Cout
  decoder_7_segmentHex decoder_7_segmenthex_1 (
    .A0(fulladd4bit_1_sum[0]), .A1(fulladd4bit_1_sum[1]), .A2(fulladd4bit_1_sum[2]), .EN(1'b1),
    .A3(fulladd4bit_1_sum[3]), .b_display(decoder_7_segmenthex_1_b_display),
    .a_display(decoder_7_segmenthex_1_a_display), .c_display(decoder_7_segmenthex_1_c_display),
    .d_display(decoder_7_segmenthex_1_d_display), .e_display(decoder_7_segmenthex_1_e_display),
    .f_display(decoder_7_segmenthex_1_f_display), .g_display(decoder_7_segmenthex_1_g_display));
  _7_Segment_Display u_7_segment_display_1 (
    .g(decoder_7_segmenthex_1_g_display), .f(decoder_7_segmenthex_1_f_display),
    .a(decoder_7_segmenthex_1_a_display), .b(decoder_7_segmenthex_1_b_display),
    .e(decoder_7_segmenthex_1_e_display), .d(decoder_7_segmenthex_1_d_display),
    .c(decoder_7_segmenthex_1_c_display));  // open: dp
endmodule
