// Logisim project compare.circ as structural Verilog: 2 circuits, main circuit compare_4bit
module compare_4bit (
  input  A0,
  input  B0,
  input  A1,
  input  B1,
  input  A2,
  input  B2,
  input  A3,
  input  B3,
  output Y
);

  wire xnor_1_out, xnor_2_out, xnor_3_out, xnor_4_out;

  xnor xnor_1 (xnor_1_out, A0, B0);
  xnor xnor_2 (xnor_2_out, A1, B1);
  xnor xnor_3 (xnor_3_out, A2, B2);
  xnor xnor_4 (xnor_4_out, A3, B3);
  and and_1 (Y, xnor_1_out, xnor_2_out, xnor_3_out, xnor_4_out);
endmodule

module compare_4bit_led (
);

  wire compare_4bit_1_y, dipswitch_1_sw1, dipswitch_1_sw2, dipswitch_1_sw3, dipswitch_1_sw4, dipswitch_2_sw1,
       dipswitch_2_sw2, dipswitch_2_sw3, dipswitch_2_sw4;

  DipSwitch #(.number(4)) dipswitch_1 (
    .sw1(dipswitch_1_sw1), .sw2(dipswitch_1_sw2), .sw3(dipswitch_1_sw3), .sw4(dipswitch_1_sw4));
  DipSwitch #(.number(4)) dipswitch_2 (
    .sw1(dipswitch_2_sw1), .sw2(dipswitch_2_sw2), .sw3(dipswitch_2_sw3), .sw4(dipswitch_2_sw4));
  compare_4bit compare_4bit_1 (
    .A0(dipswitch_1_sw1), .B0(dipswitch_2_sw1), .A1(dipswitch_1_sw2), .B1(dipswitch_2_sw2),
    .A2(dipswitch_1_sw3), .B2(dipswitch_2_sw3), .A3(dipswitch_1_sw4), .B3(dipswitch_2_sw4),
    .Y(compare_4bit_1_y));
  LED led_1 (.in(compare_4bit_1_y));
endmodule
