// Logisim project decoder.circ as structural Verilog: 6 circuits, main circuit decoder2_4_1bit
module decoder2_4_1bit (
  input  A0,
  input  A1,
  input  EN,
  output Y0,
  output Y1,
  output Y2,
  output Y3
);

  wire not_1_out, not_2_out;

  not not_1 (not_1_out, A0);
  not not_2 (not_2_out, A1);
  and and_1 (Y0, not_1_out, EN, not_2_out);
  and and_2 (Y1, A0, EN, not_2_out);
  and and_3 (Y2, not_1_out, EN, A1);
  and and_4 (Y3, A0, EN, A1);
endmodule

module decoder3_8_1bit (
  input  A0,
  input  A1,
  input  A2,
  input  EN,
  output Y0,
  output Y1,
  output Y2,
  output Y3,
  output Y4,
  output Y5,
  output Y6,
  output Y7
);

  wire and_1_out, and_2_out, not_1_out;

  not not_1 (not_1_out, A2);
  and and_1 (and_1_out, not_1_out, EN);
  and and_2 (and_2_out, A2, EN);
  decoder2_4_1bit decoder2_4_1bit_1 (.A0(A0), .A1(A1), .EN(and_1_out), .Y0(Y0), .Y1(Y1), .Y2(Y2), .Y3(Y3));
  decoder2_4_1bit decoder2_4_1bit_2 (.A0(A0), .A1(A1), .EN(and_2_out), .Y0(Y4), .Y1(Y5), .Y2(Y6), .Y3(Y7));
endmodule

module decoder_7_segment (
  input  A0,
  input  A1,
  input  A2,
  input  EN,
  input  A3
);

  wire a_out, and_1_out, and_2_out, b_out, c_out, d_out, decoder3_8_1bit_1_y0, decoder3_8_1bit_1_y1,
       decoder3_8_1bit_1_y2, decoder3_8_1bit_1_y3, decoder3_8_1bit_1_y4, decoder3_8_1bit_1_y5,
       decoder3_8_1bit_1_y6, decoder3_8_1bit_1_y7, decoder3_8_1bit_2_y0, decoder3_8_1bit_2_y1,
       decoder3_8_1bit_2_y2, decoder3_8_1bit_2_y3, decoder3_8_1bit_2_y4, decoder3_8_1bit_2_y5,
       decoder3_8_1bit_2_y6, decoder3_8_1bit_2_y7, e_out, f_out, g_out, not_1_out, or_1_out;

  and and_1 (and_1_out, EN, not_1_out);
  not not_1 (not_1_out, A3);
  and and_2 (and_2_out, EN, A3);
  decoder3_8_1bit decoder3_8_1bit_1 (
    .A0(A0), .A1(A1), .A2(A2), .EN(and_1_out), .Y0(decoder3_8_1bit_1_y0), .Y1(decoder3_8_1bit_1_y1),
    .Y2(decoder3_8_1bit_1_y2), .Y3(decoder3_8_1bit_1_y3), .Y4(decoder3_8_1bit_1_y4),
    .Y5(decoder3_8_1bit_1_y5), .Y6(decoder3_8_1bit_1_y6), .Y7(decoder3_8_1bit_1_y7));
  decoder3_8_1bit decoder3_8_1bit_2 (
    .A0(A0), .A1(A1), .A2(A2), .EN(and_2_out), .Y0(decoder3_8_1bit_2_y0), .Y1(decoder3_8_1bit_2_y1),
    .Y2(decoder3_8_1bit_2_y2), .Y3(decoder3_8_1bit_2_y3), .Y4(decoder3_8_1bit_2_y4),
    .Y5(decoder3_8_1bit_2_y5), .Y6(decoder3_8_1bit_2_y6), .Y7(decoder3_8_1bit_2_y7));
  or or_1 (or_1_out, decoder3_8_1bit_2_y7, decoder3_8_1bit_2_y6, decoder3_8_1bit_2_y5, decoder3_8_1bit_2_y4, decoder3_8_1bit_2_y3, decoder3_8_1bit_2_y2);
  or a (a_out, decoder3_8_1bit_2_y1, decoder3_8_1bit_2_y0, decoder3_8_1bit_1_y7, decoder3_8_1bit_1_y6, decoder3_8_1bit_1_y5, decoder3_8_1bit_1_y3, decoder3_8_1bit_1_y2, decoder3_8_1bit_1_y0);
  _7_Segment_Display u_7_segment_display_1 (
    .g(g_out), .f(f_out), .a(a_out), .b(b_out), .e(e_out), .d(d_out), .c(c_out), .dp(or_1_out));
  or b (b_out, decoder3_8_1bit_2_y1, decoder3_8_1bit_2_y0, decoder3_8_1bit_1_y7, decoder3_8_1bit_1_y4, decoder3_8_1bit_1_y3, decoder3_8_1bit_1_y2, decoder3_8_1bit_1_y1, decoder3_8_1bit_1_y0);
  or c (c_out, decoder3_8_1bit_2_y1, decoder3_8_1bit_2_y0, decoder3_8_1bit_1_y7, decoder3_8_1bit_1_y6, decoder3_8_1bit_1_y5, decoder3_8_1bit_1_y4, decoder3_8_1bit_1_y3, decoder3_8_1bit_1_y1, decoder3_8_1bit_1_y0);
  or d (d_out, decoder3_8_1bit_2_y1, decoder3_8_1bit_2_y0, decoder3_8_1bit_1_y6, decoder3_8_1bit_1_y5, decoder3_8_1bit_1_y3, decoder3_8_1bit_1_y2, decoder3_8_1bit_1_y0);
  or e (e_out, decoder3_8_1bit_2_y0, decoder3_8_1bit_1_y6, decoder3_8_1bit_1_y2, decoder3_8_1bit_1_y0);
  or f (f_out, decoder3_8_1bit_2_y1, decoder3_8_1bit_2_y0, decoder3_8_1bit_1_y6, decoder3_8_1bit_1_y5, decoder3_8_1bit_1_y4, decoder3_8_1bit_1_y0);
  or g (g_out, decoder3_8_1bit_2_y1, decoder3_8_1bit_2_y0, decoder3_8_1bit_1_y6, decoder3_8_1bit_1_y5, decoder3_8_1bit_1_y4, decoder3_8_1bit_1_y3, decoder3_8_1bit_1_y2);
endmodule

module decoder_7_segmentHex (
  input  A0,
  input  A1,
  input  A2,
  input  EN,
  input  A3,
  output b_display,
  output a_display,
  output c_display,
  output d_display,
  output e_display,
  output f_display,
  output g_display
);

  wire and_1_out, and_2_out, decoder3_8_1bit_1_y0, decoder3_8_1bit_1_y1, decoder3_8_1bit_1_y2,
       decoder3_8_1bit_1_y3, decoder3_8_1bit_1_y4, decoder3_8_1bit_1_y5, decoder3_8_1bit_1_y6,
       decoder3_8_1bit_1_y7, decoder3_8_1bit_2_y0, decoder3_8_1bit_2_y1, decoder3_8_1bit_2_y2,
       decoder3_8_1bit_2_y3, decoder3_8_1bit_2_y4, decoder3_8_1bit_2_y5, decoder3_8_1bit_2_y6,
       decoder3_8_1bit_2_y7, not_1_out;

  and and_1 (and_1_out, EN, not_1_out);
  not not_1 (not_1_out, A3);
  and and_2 (and_2_out, EN, A3);
  decoder3_8_1bit decoder3_8_1bit_1 (
    .A0(A0), .A1(A1), .A2(A2), .EN(and_1_out), .Y0(decoder3_8_1bit_1_y0), .Y1(decoder3_8_1bit_1_y1),
    .Y2(decoder3_8_1bit_1_y2), .Y3(decoder3_8_1bit_1_y3), .Y4(decoder3_8_1bit_1_y4),
    .Y5(decoder3_8_1bit_1_y5), .Y6(decoder3_8_1bit_1_y6), .Y7(decoder3_8_1bit_1_y7));
  decoder3_8_1bit decoder3_8_1bit_2 (
    .A0(A0), .A1(A1), .A2(A2), .EN(and_2_out), .Y0(decoder3_8_1bit_2_y0), .Y1(decoder3_8_1bit_2_y1),
    .Y2(decoder3_8_1bit_2_y2), .Y3(decoder3_8_1bit_2_y3), .Y4(decoder3_8_1bit_2_y4),
    .Y5(decoder3_8_1bit_2_y5), .Y6(decoder3_8_1bit_2_y6), .Y7(decoder3_8_1bit_2_y7));
  or a (a_display, decoder3_8_1bit_2_y7, decoder3_8_1bit_2_y6, decoder3_8_1bit_2_y4, decoder3_8_1bit_2_y2, decoder3_8_1bit_2_y1, decoder3_8_1bit_2_y0, decoder3_8_1bit_1_y7, decoder3_8_1bit_1_y6, decoder3_8_1bit_1_y5, decoder3_8_1bit_1_y3, decoder3_8_1bit_1_y2, decoder3_8_1bit_1_y0);
  or b (b_display, decoder3_8_1bit_2_y5, decoder3_8_1bit_2_y2, decoder3_8_1bit_2_y1, decoder3_8_1bit_2_y0, decoder3_8_1bit_1_y7, decoder3_8_1bit_1_y4, decoder3_8_1bit_1_y3, decoder3_8_1bit_1_y2, decoder3_8_1bit_1_y1, decoder3_8_1bit_1_y0);
  or c (c_display, decoder3_8_1bit_2_y5, decoder3_8_1bit_2_y3, decoder3_8_1bit_2_y2, decoder3_8_1bit_2_y1, decoder3_8_1bit_2_y0, decoder3_8_1bit_1_y7, decoder3_8_1bit_1_y6, decoder3_8_1bit_1_y5, decoder3_8_1bit_1_y4, decoder3_8_1bit_1_y3, decoder3_8_1bit_1_y1, decoder3_8_1bit_1_y0);
  or d (d_display, decoder3_8_1bit_2_y6, decoder3_8_1bit_2_y5, decoder3_8_1bit_2_y4, decoder3_8_1bit_2_y3, decoder3_8_1bit_2_y1, decoder3_8_1bit_2_y0, decoder3_8_1bit_1_y6, decoder3_8_1bit_1_y5, decoder3_8_1bit_1_y3, decoder3_8_1bit_1_y2, decoder3_8_1bit_1_y0);
  or e (e_display, decoder3_8_1bit_2_y7, decoder3_8_1bit_2_y6, decoder3_8_1bit_2_y5, decoder3_8_1bit_2_y4, decoder3_8_1bit_2_y3, decoder3_8_1bit_2_y2, decoder3_8_1bit_2_y0, decoder3_8_1bit_1_y6, decoder3_8_1bit_1_y2, decoder3_8_1bit_1_y0);
  or f (f_display, decoder3_8_1bit_2_y7, decoder3_8_1bit_2_y6, decoder3_8_1bit_2_y4, decoder3_8_1bit_2_y3, decoder3_8_1bit_2_y2, decoder3_8_1bit_2_y1, decoder3_8_1bit_2_y0, decoder3_8_1bit_1_y6, decoder3_8_1bit_1_y5, decoder3_8_1bit_1_y4, decoder3_8_1bit_1_y0);
  or g (g_display, decoder3_8_1bit_2_y7, decoder3_8_1bit_2_y6, decoder3_8_1bit_2_y5, decoder3_8_1bit_2_y3, decoder3_8_1bit_2_y2, decoder3_8_1bit_2_y1, decoder3_8_1bit_2_y0, decoder3_8_1bit_1_y6, decoder3_8_1bit_1_y5, decoder3_8_1bit_1_y4, decoder3_8_1bit_1_y3, decoder3_8_1bit_1_y2);
endmodule

module decoder_7_segmenthex_display (
  input  in_1
);

  wire decoder_7_segmenthex_1_a_display, decoder_7_segmenthex_1_b_display, decoder_7_segmenthex_1_c_display,
       decoder_7_segmenthex_1_d_display, decoder_7_segmenthex_1_e_display, decoder_7_segmenthex_1_f_display,
       decoder_7_segmenthex_1_g_display, dipswitch_1_sw1, dipswitch_1_sw2, dipswitch_1_sw3, dipswitch_1_sw4;

  DipSwitch #(.number(4)) dipswitch_1 (
    .sw1(dipswitch_1_sw1), .sw2(dipswitch_1_sw2), .sw3(dipswitch_1_sw3), .sw4(dipswitch_1_sw4));
  decoder_7_segmentHex decoder_7_segmenthex_1 (
    .A0(dipswitch_1_sw1), .A1(dipswitch_1_sw2), .A2(dipswitch_1_sw3), .EN(in_1), .A3(dipswitch_1_sw4),
    .b_display(decoder_7_segmenthex_1_b_display), .a_display(decoder_7_segmenthex_1_a_display),
    .c_display(decoder_7_segmenthex_1_c_display), .d_display(decoder_7_segmenthex_1_d_display),
    .e_display(decoder_7_segmenthex_1_e_display), .f_display(decoder_7_segmenthex_1_f_display),
    .g_display(decoder_7_segmenthex_1_g_display));
  _7_Segment_Display u_7_segment_display_1 (
    .g(decoder_7_segmenthex_1_g_display), .f(decoder_7_segmenthex_1_f_display),
    .a(decoder_7_segmenthex_1_a_display), .b(decoder_7_segmenthex_1_b_display),
    .e(decoder_7_segmenthex_1_e_display), .d(decoder_7_segmenthex_1_d_display),
    .c(decoder_7_segmenthex_1_c_display));  // open: dp
endmodule

module decoder1_2_1bit (
  input  A,
  input  EN,
  output Y0,
  output Y1
);

  wire not_1_out;

  not not_1 (not_1_out, A);
  and and_1 (Y0, not_1_out, EN);
  and and_2 (Y1, A, EN);
endmodule
