// Logisim project encoder.circ as structural Verilog: 4 circuits, main circuit encoder4_2
module encoder4_2 (
  input  A0,
  input  A1,
  input  A2,
  input  A3,
  input  EN,
  output Y0,
  output Y1
);

  wire or_1_out, or_2_out;

  or or_1 (or_1_out, A3, A1);
  or or_2 (or_2_out, A2, A3);
  and and_1 (Y0, or_1_out, EN);
  and and_2 (Y1, or_2_out, EN);
endmodule

module encoder16_4 (
  input  EN,
  input  A0,
  input  A1,
  input  A2,
  input  A3,
  input  A4,
  input  A5,
  input  A6,
  input  A7,
  input  A8,
  input  A9,
  input  A10,
  input  A11,
  input  A12,
  input  A13,
  input  A14,
  input  A15,
  output Y0,
  output Y1,
  output Y2,
  output Y3
);

  wire or_1_out, or_2_out, or_3_out, or_4_out;

  or or_1 (or_1_out, A1, A3, A5, A7, A9, A11, A13, A15);
  or or_2 (or_2_out, A14, A11, A2, A3, A6, A7, A10, A15);
  or or_3 (or_3_out, A13, A4, A5, A6, A7, A12, A15, A14);
  or or_4 (or_4_out, A8, A9, A10, A11, A12, A13, A14, A15);
  and and_1 (Y0, EN, or_1_out);
  and and_2 (Y1, EN, or_2_out);
  and and_3 (Y2, EN, or_3_out);
  and and_4 (Y3, EN, or_4_out);
endmodule

module encoder16_4_display (
  input  in_1
);

  wire decoder_7_segmenthex_1_a_display, decoder_7_segmenthex_1_b_display, decoder_7_segmenthex_1_c_display,
       decoder_7_segmenthex_1_d_display, decoder_7_segmenthex_1_e_display, decoder_7_segmenthex_1_f_display,
       decoder_7_segmenthex_1_g_display, dipswitch_1_sw1, dipswitch_1_sw2, dipswitch_1_sw3, dipswitch_1_sw4,
       dipswitch_1_sw5, dipswitch_1_sw6, dipswitch_1_sw7, dipswitch_1_sw8, dipswitch_1_sw9, dipswitch_1_sw10,
       dipswitch_1_sw11, dipswitch_1_sw12, dipswitch_1_sw13, dipswitch_1_sw14, dipswitch_1_sw15,
       dipswitch_1_sw16, encoder16_4_1_y0, encoder16_4_1_y1, encoder16_4_1_y2, encoder16_4_1_y3;

  DipSwitch #(.number(16)) dipswitch_1 (
    .sw1(dipswitch_1_sw1), .sw2(dipswitch_1_sw2), .sw3(dipswitch_1_sw3), .sw4(dipswitch_1_sw4),
    .sw5(dipswitch_1_sw5), .sw6(dipswitch_1_sw6), .sw7(dipswitch_1_sw7), .sw8(dipswitch_1_sw8),
    .sw9(dipswitch_1_sw9), .sw10(dipswitch_1_sw10), .sw11(dipswitch_1_sw11), .sw12(dipswitch_1_sw12),
    .sw13(dipswitch_1_sw13), .sw14(dipswitch_1_sw14), .sw15(dipswitch_1_sw15), .sw16(dipswitch_1_sw16));
  encoder16_4 encoder16_4_1 (
    .EN(in_1), .A0(dipswitch_1_sw1), .A1(dipswitch_1_sw2), .A2(dipswitch_1_sw3), .A3(dipswitch_1_sw4),
    .A4(dipswitch_1_sw5), .A5(dipswitch_1_sw6), .A6(dipswitch_1_sw7), .A7(dipswitch_1_sw8),
    .A8(dipswitch_1_sw9), .A9(dipswitch_1_sw10), .A10(dipswitch_1_sw11), .A11(dipswitch_1_sw12),
    .A12(dipswitch_1_sw13), .A13(dipswitch_1_sw14), .A14(dipswitch_1_sw15), .A15(dipswitch_1_sw16),
    .Y0(encoder16_4_1_y0), .Y1(encoder16_4_1_y1), .Y2(encoder16_4_1_y2), .Y3(encoder16_4_1_y3));
  decoder_7_segmentHex decoder_7_segmenthex_1 (
    .A0(encoder16_4_1_y0), .A1(encoder16_4_1_y1), .A2(encoder16_4_1_y2), .EN(in_1), .A3(encoder16_4_1_y3),
    .b_display(decoder_7_segmenthex_1_b_display), .a_display(decoder_7_segmenthex_1_a_display),
    .c_display(decoder_7_segmenthex_1_c_display), .d_display(decoder_7_segmenthex_1_d_display),
    .e_display(decoder_7_segmenthex_1_e_display), .f_display(decoder_7_segmenthex_1_f_display),
    .g_display(decoder_7_segmenthex_1_g_display));
  _7_Segment_Display u_7_segment_display_1 (
    .g(decoder_7_segmenthex_1_g_display), .f(decoder_7_segmenthex_1_f_display),
    .a(decoder_7_segmenthex_1_a_display), .b(decoder_7_segmenthex_1_b_display),
    .e(decoder_7_segmenthex_1_e_display), .d(decoder_7_segmenthex_1_d_display),
    .c(decoder_7_segmenthex_1_c_display));  // open: dp
endmodule

module p_encder4_2 (
  input  A3,
  input  A2,
  input  A1,
  input  A0,
  output Y0,
  output Y1
);

  wire and_1_out, and_2_out, not_1_out, not_2_out;

  not not_1 (not_1_out, A3);
  not not_2 (not_2_out, A2);
  and and_1 (and_1_out, not_1_out, A2);
  and and_2 (and_2_out, A1, not_2_out, not_1_out);
  or or_1 (Y0, and_1_out, A3);
  or or_2 (Y1, and_2_out, A3);
endmodule
