// Logisim project mux.circ as structural Verilog: 5 circuits, main circuit mux_2_1
module mux_2_1 (
  input  D0,
  input  A,
  input  EN,
  input  D1,
  output Y
);

  wire and_1_out, and_2_out, decoder1_2_1bit_1_y0, decoder1_2_1bit_1_y1;

  decoder1_2_1bit decoder1_2_1bit_1 (.A(A), .EN(EN), .Y0(decoder1_2_1bit_1_y0), .Y1(decoder1_2_1bit_1_y1));
  and and_1 (and_1_out, D0, decoder1_2_1bit_1_y0);
  and and_2 (and_2_out, decoder1_2_1bit_1_y1, D1);
  or or_1 (Y, and_1_out, and_2_out);
endmodule

module mux_4_1_3bit (
  input  [2:0] D0,
  input  [2:0] D1,
  input  [2:0] D2,
  input  [2:0] D3,
  input  EN,
  input  [1:0] A,
  output [2:0] Y
);

  mux_4_1_1bit mux_4_1_1bit_1 (.D0(D0[0]), .D1(D1[0]), .A0(A[0]), .A1(A[1]), .EN(EN), .D2(D2[0]), .D3(D3[0]), .Y(Y[0]));
  mux_4_1_1bit mux_4_1_1bit_2 (.D0(D0[1]), .D1(D1[1]), .A0(A[0]), .A1(A[1]), .EN(EN), .D2(D2[1]), .D3(D3[1]), .Y(Y[1]));
  mux_4_1_1bit mux_4_1_1bit_3 (.D0(D0[2]), .D1(D1[2]), .A0(A[0]), .A1(A[1]), .EN(EN), .D2(D2[2]), .D3(D3[2]), .Y(Y[2]));
endmodule

module mux_4_1_1bit (
  input  D0,
  input  D1,
  input  A0,
  input  A1,
  input  EN,
  input  D2,
  input  D3,
  output Y
);

  wire and_1_out, and_2_out, and_3_out, and_4_out, decoder2_4_1bit_1_y0, decoder2_4_1bit_1_y1,
       decoder2_4_1bit_1_y2, decoder2_4_1bit_1_y3;

  decoder2_4_1bit decoder2_4_1bit_1 (
    .A0(A0), .A1(A1), .EN(EN), .Y0(decoder2_4_1bit_1_y0), .Y1(decoder2_4_1bit_1_y1),
    .Y2(decoder2_4_1bit_1_y2), .Y3(decoder2_4_1bit_1_y3));
  and and_1 (and_1_out, D0, decoder2_4_1bit_1_y0);
  and and_2 (and_2_out, D1, decoder2_4_1bit_1_y1);
  and and_3 (and_3_out, decoder2_4_1bit_1_y2, D2);
  and and_4 (and_4_out, decoder2_4_1bit_1_y3, D3);
  or or_1 (Y, and_1_out, and_2_out, and_3_out, and_4_out);
endmodule

module mux_2_1_display (
);

  wire decoder7_1_a_s, decoder7_1_b_s, decoder7_1_c_s, decoder7_1_d_s, decoder7_1_e_s, decoder7_1_f_s,
       decoder7_1_g_s, decoder7_1_o_s, decoder_7_segmenthex_1_a_display, decoder_7_segmenthex_1_b_display,
       decoder_7_segmenthex_1_c_display, decoder_7_segmenthex_1_d_display, decoder_7_segmenthex_1_e_display,
       decoder_7_segmenthex_1_f_display, decoder_7_segmenthex_1_g_display, dipswitch_1_sw1, dipswitch_1_sw2,
       dipswitch_1_sw3, dipswitch_1_sw4, dipswitch_1_sw5, mux_2_1_1_y, not_1_out;

  DipSwitch #(.number(5)) dipswitch_1 (
    .sw1(dipswitch_1_sw1), .sw2(dipswitch_1_sw2), .sw3(dipswitch_1_sw3), .sw4(dipswitch_1_sw4),
    .sw5(dipswitch_1_sw5));
  mux_2_1 mux_2_1_1 (.D0(1'b1), .A(dipswitch_1_sw1), .EN(1'b1), .D1(1'b0), .Y(mux_2_1_1_y));
  not not_1 (not_1_out, mux_2_1_1_y);
  decoder7 decoder7_1 (
    .A0(dipswitch_1_sw2), .A1(dipswitch_1_sw3), .A2(dipswitch_1_sw4), .EN(mux_2_1_1_y), .A3(dipswitch_1_sw5),
    .a_s(decoder7_1_a_s), .b_s(decoder7_1_b_s), .c_s(decoder7_1_c_s), .d_s(decoder7_1_d_s),
    .e_s(decoder7_1_e_s), .f_s(decoder7_1_f_s), .g_s(decoder7_1_g_s), .o_s(decoder7_1_o_s));
  decoder_7_segmentHex decoder_7_segmenthex_1 (
    .A0(dipswitch_1_sw2), .A1(dipswitch_1_sw3), .A2(dipswitch_1_sw4), .EN(not_1_out), .A3(dipswitch_1_sw5),
    .b_display(decoder_7_segmenthex_1_b_display), .a_display(decoder_7_segmenthex_1_a_display),
    .c_display(decoder_7_segmenthex_1_c_display), .d_display(decoder_7_segmenthex_1_d_display),
    .e_display(decoder_7_segmenthex_1_e_display), .f_display(decoder_7_segmenthex_1_f_display),
    .g_display(decoder_7_segmenthex_1_g_display));
  _7_Segment_Display u_7_segment_display_1 (
    .g(decoder_7_segmenthex_1_g_display), .f(decoder_7_segmenthex_1_f_display),
    .a(decoder_7_segmenthex_1_a_display), .b(decoder_7_segmenthex_1_b_display),
    .e(decoder_7_segmenthex_1_e_display), .d(decoder_7_segmenthex_1_d_display),
    .c(decoder_7_segmenthex_1_c_display));  // open: dp
  _7_Segment_Display u_7_segment_display_2 (
    .g(decoder7_1_g_s), .f(decoder7_1_f_s), .a(decoder7_1_a_s), .b(decoder7_1_b_s), .e(decoder7_1_e_s),
    .d(decoder7_1_d_s), .c(decoder7_1_c_s), .dp(decoder7_1_o_s));
endmodule

module decoder7 (
  input  A0,
  input  A1,
  input  A2,
  input  EN,
  input  A3,
  output a_s,
  output b_s,
  output c_s,
  output d_s,
  output e_s,
  output f_s,
  output g_s,
  output o_s
);

  wire and_1_out, and_2_out, decoder3_8_1bit_1_y0, decoder3_8_1bit_1_y1, decoder3_8_1bit_1_y2,
       decoder3_8_1bit_1_y3, decoder3_8_1bit_1_y4, decoder3_8_1bit_1_y5, decoder3_8_1bit_1_y6,
       decoder3_8_1bit_1_y7, decoder3_8_1bit_2_y0, decoder3_8_1bit_2_y1, decoder3_8_1bit_2_y2,
       decoder3_8_1bit_2_y3, decoder3_8_1bit_2_y4, decoder3_8_1bit_2_y5, decoder3_8_1bit_2_y6,
       decoder3_8_1bit_2_y7, not_1_out;

  and and_1 (and_1_out, EN, not_1_out);
  not not_1 (not_1_out, A3);
  and and_2 (and_2_out, EN, A3);
  decoder3_8_1bit decoder3_8_1bit_1 (
    .A0(A0), .A1(A1), .A2(A2), .EN(and_1_out), .Y0(decoder3_8_1bit_1_y0), .Y1(decoder3_8_1bit_1_y1),
    .Y2(decoder3_8_1bit_1_y2), .Y3(decoder3_8_1bit_1_y3), .Y4(decoder3_8_1bit_1_y4),
    .Y5(decoder3_8_1bit_1_y5), .Y6(decoder3_8_1bit_1_y6), .Y7(decoder3_8_1bit_1_y7));
  decoder3_8_1bit decoder3_8_1bit_2 (
    .A0(A0), .A1(A1), .A2(A2), .EN(and_2_out), .Y0(decoder3_8_1bit_2_y0), .Y1(decoder3_8_1bit_2_y1),
    .Y2(decoder3_8_1bit_2_y2), .Y3(decoder3_8_1bit_2_y3), .Y4(decoder3_8_1bit_2_y4),
    .Y5(decoder3_8_1bit_2_y5), .Y6(decoder3_8_1bit_2_y6), .Y7(decoder3_8_1bit_2_y7));
  or or_1 (o_s, decoder3_8_1bit_2_y7, decoder3_8_1bit_2_y6, decoder3_8_1bit_2_y5, decoder3_8_1bit_2_y4, decoder3_8_1bit_2_y3, decoder3_8_1bit_2_y2);
  or a (a_s, decoder3_8_1bit_2_y1, decoder3_8_1bit_2_y0, decoder3_8_1bit_1_y7, decoder3_8_1bit_1_y6, decoder3_8_1bit_1_y5, decoder3_8_1bit_1_y3, decoder3_8_1bit_1_y2, decoder3_8_1bit_1_y0);
  _7_Segment_Display u_7_segment_display_1 (.g(g_s), .f(f_s), .a(a_s), .b(b_s), .e(e_s), .d(d_s), .c(c_s), .dp(o_s));
  or b (b_s, decoder3_8_1bit_2_y1, decoder3_8_1bit_2_y0, decoder3_8_1bit_1_y7, decoder3_8_1bit_1_y4, decoder3_8_1bit_1_y3, decoder3_8_1bit_1_y2, decoder3_8_1bit_1_y1, decoder3_8_1bit_1_y0);
  or c (c_s, decoder3_8_1bit_2_y1, decoder3_8_1bit_2_y0, decoder3_8_1bit_1_y7, decoder3_8_1bit_1_y6, decoder3_8_1bit_1_y5, decoder3_8_1bit_1_y4, decoder3_8_1bit_1_y3, decoder3_8_1bit_1_y1, decoder3_8_1bit_1_y0);
  or d (d_s, decoder3_8_1bit_2_y1, decoder3_8_1bit_2_y0, decoder3_8_1bit_1_y6, decoder3_8_1bit_1_y5, decoder3_8_1bit_1_y3, decoder3_8_1bit_1_y2, decoder3_8_1bit_1_y0);
  or e (e_s, decoder3_8_1bit_2_y0, decoder3_8_1bit_1_y6, decoder3_8_1bit_1_y2, decoder3_8_1bit_1_y0);
  or f (f_s, decoder3_8_1bit_2_y1, decoder3_8_1bit_2_y0, decoder3_8_1bit_1_y6, decoder3_8_1bit_1_y5, decoder3_8_1bit_1_y4, decoder3_8_1bit_1_y0);
  or g (g_s, decoder3_8_1bit_2_y1, decoder3_8_1bit_2_y0, decoder3_8_1bit_1_y6, decoder3_8_1bit_1_y5, decoder3_8_1bit_1_y4, decoder3_8_1bit_1_y3, decoder3_8_1bit_1_y2);
endmodule
